# Fritzing sketch AVR_int1 (saved by Fritzing 0.9.3b)
breadboards: 1

parts:
  Part1 = Arduino Uno (Rev3)
  LED1 = LED - 5mm [color="Red (633nm)" package="5 mm [THT]"]
  LED2 = LED - 5mm [color="Red (633nm)" package="5 mm [THT]"]
  R1 = Resistor [tolerance=±5% resistance=330 package=THT]
  R2 = Resistor [tolerance=±5% resistance=330 package=THT]
  S1 = Pushbutton [package="[THT]"]

nets:
  N1: Part1.D13/SCK, R1.Pin_0
  N2: Part1.GND, LED1.cathode, LED2.cathode, S1.Pin_1, S1.Pin_2
  N3: Part1.D3_PWM, S1.Pin_3, S1.Pin_4
  N4: Part1.D5_PWM, R2.Pin_0
  N5: LED1.anode, R1.Pin_1
  N6: LED2.anode, R2.Pin_1

notes:
  D13 LED
  D5 LED
  D13
  GND
  D5
  D3
